// Logisim project 16to1BITMULTIPLEXER.circ as structural Verilog: 1 circuit, main circuit main
module main (
  input  in_1,
  input  in_2,
  input  in_3,
  input  in_4,
  input  in_5,
  input  in_6,
  input  in_7,
  input  in_8,
  input  [1:0] in_9,
  input  in_10,
  input  in_11,
  input  in_12,
  input  in_13,
  input  in_14,
  input  in_15,
  input  in_16,
  input  in_17,
  input  in_18,
  input  [1:0] in_19,
  input  in_20,
  output out_21
);

  wire multiplexer_1_out, multiplexer_2_out, multiplexer_3_out, multiplexer_4_out;

  Multiplexer #(.select(2)) multiplexer_1 (
    .in0(in_1), .in1(in_2), .in2(in_3), .in3(in_4), .out(multiplexer_1_out), .sel(in_19), .en(in_20));
  Multiplexer #(.select(2)) multiplexer_2 (
    .in0(in_5), .in1(in_6), .in2(in_7), .in3(in_8), .out(multiplexer_2_out), .sel(in_19), .en(in_20));
  Multiplexer #(.select(2)) multiplexer_3 (
    .in0(in_10), .in1(in_11), .in2(in_12), .in3(in_14), .out(multiplexer_3_out), .sel(in_19), .en(in_20));
  Multiplexer #(.select(2)) multiplexer_4 (
    .in0(in_15), .in1(in_16), .in2(in_17), .in3(in_18), .out(multiplexer_4_out), .sel(in_19), .en(in_20));
  Multiplexer #(.select(2)) multiplexer_5 (
    .in0(multiplexer_1_out), .in1(multiplexer_2_out), .in2(multiplexer_3_out), .in3(multiplexer_4_out),
    .out(out_21), .sel(in_9), .en(in_13));
endmodule
