// Logisim project 2TO4_DECODER.circ as structural Verilog: 1 circuit, main circuit main
module main (
  input  A,
  input  B,
  input  in_3,
  input  [1:0] in_4,
  output out_5,
  output out_6,
  output out_7,
  output out_8,
  output out_9,
  output out_10,
  output out_11,
  output out_12
);

  wire not_1_out, not_2_out;

  not not_1 (not_1_out, A);
  not not_2 (not_2_out, B);
  and and_1 (out_6, not_1_out, not_2_out);
  and and_2 (out_9, not_1_out, B);
  and and_3 (out_11, A, not_2_out);
  and and_4 (out_12, A, B);
  Decoder #(.select(2)) decoder_1 (.out0(out_5), .out1(out_7), .out2(out_8), .out3(out_10), .sel(in_4), .en(in_3));

  // Notes on the sheet:
  //   A'B
  //   AB'
  //   A'B'
  //   AB
endmodule
