// Logisim project 4BITs_ALU.circ as structural Verilog: 1 circuit, main circuit main
module main (
  input  [3:0] A,
  input  [3:0] B,
  input  [2:0] ALUOp,
  output [3:0] Result
);

  wire adder_1_cout;
  wire [3:0] adder_1_out, and_1_out, or_1_out, subtractor_1_out, xor_1_out;

  Adder #(.width(4)) adder_1 (.a(A), .out(adder_1_out), .cout(adder_1_cout));  // open: b, cin
  Subtractor #(.width(4)) subtractor_1 (.a(B), .b(B), .out(subtractor_1_out), .bin(adder_1_cout));  // open: bout
  assign and_1_out = B;  // AND_Gate and_1, 4 bits wide AND_Gate
  assign or_1_out = B;  // OR_Gate or_1, 4 bits wide OR_Gate
  assign xor_1_out = B;  // XOR_Gate xor_1, 4 bits wide XOR_Gate
  Multiplexer #(.select(3), .width(4)) multiplexer_1 (
    .in2(adder_1_out), .in3(or_1_out), .in4(xor_1_out), .in5(subtractor_1_out), .in6(and_1_out),
    .out(Result), .sel(ALUOp));  // open: in0, in1, in7, en
endmodule
