// Logisim project 4bits_syncorince_counter.circ as structural Verilog: 1 circuit, main circuit main
module main (
  input  in_1,
  input  CLEAR,
  output Q2,
  output Q1,
  output Q0,
  output Q3
);

  wire and_1_out, and_2_out, clock_1_out;

  Clock clock_1 (.out(clock_1_out));
  J_K_Flip_Flop j_k_ff_1 (.J(in_1), .clk(clock_1_out), .K(in_1), .Q(Q0), .reset(CLEAR));  // open: Qn, preset, en
  J_K_Flip_Flop j_k_ff_2 (.J(Q0), .clk(clock_1_out), .K(Q0), .Q(Q1), .reset(CLEAR));  // open: Qn, preset, en
  and and_1 (and_1_out, Q0, Q1);
  J_K_Flip_Flop j_k_ff_3 (
    .J(and_1_out), .clk(clock_1_out), .K(and_1_out), .Q(Q2), .reset(CLEAR));  // open: Qn, preset, en
  and and_2 (and_2_out, and_1_out, Q2);
  J_K_Flip_Flop j_k_ff_4 (
    .J(and_2_out), .clk(clock_1_out), .K(and_2_out), .Q(Q3), .reset(CLEAR));  // open: Qn, preset, en

  // Notes on the sheet:
  //   SERIAL INPUT
  //   CLOCK
  //   4BIT SYNCHROUNOUS UP COUNTER
endmodule
