// Logisim project 8BIT_ADDER_SUBTRACTOR.circ as structural Verilog: 1 circuit, main circuit main
module main (
  input  K,
  input  A0,
  input  B0,
  input  A1,
  input  B1,
  input  A2,
  input  B2,
  input  A3,
  input  B3,
  input  A4,
  input  B4,
  input  A5,
  input  B5,
  input  A6,
  input  B6,
  input  A7,
  input  B7,
  output S0,
  output S1,
  output S2,
  output S3,
  output S4,
  output S5,
  output S6,
  output S7,
  output COUNT
);

  wire adder_1_cout, adder_2_cout, adder_3_cout, adder_4_cout, adder_5_cout, adder_6_cout, adder_7_cout,
       xor_1_out, xor_2_out, xor_3_out, xor_4_out, xor_5_out, xor_6_out, xor_7_out, xor_8_out;

  xor xor_1 (xor_1_out, K, B0);
  xor xor_2 (xor_2_out, K, B1);
  xor xor_3 (xor_3_out, K, B2);
  xor xor_4 (xor_4_out, K, B3);
  xor xor_5 (xor_5_out, K, B4);
  xor xor_6 (xor_6_out, K, B5);
  xor xor_7 (xor_7_out, K, B6);
  xor xor_8 (xor_8_out, K, B7);
  Adder #(.width(1)) adder_1 (.a(A0), .b(xor_1_out), .out(S0), .cin(K), .cout(adder_1_cout));
  Adder #(.width(1)) adder_2 (.a(A1), .b(xor_2_out), .out(S1), .cin(adder_1_cout), .cout(adder_2_cout));
  Adder #(.width(1)) adder_3 (.a(A2), .b(xor_3_out), .out(S2), .cin(adder_2_cout), .cout(adder_3_cout));
  Adder #(.width(1)) adder_4 (.a(A3), .b(xor_4_out), .out(S3), .cin(adder_3_cout), .cout(adder_4_cout));
  Adder #(.width(1)) adder_5 (.a(A4), .b(xor_5_out), .out(S4), .cin(adder_4_cout), .cout(adder_5_cout));
  Adder #(.width(1)) adder_6 (.a(A5), .b(xor_6_out), .out(S5), .cin(adder_5_cout), .cout(adder_6_cout));
  Adder #(.width(1)) adder_7 (.a(A6), .b(xor_7_out), .out(S6), .cin(adder_6_cout), .cout(adder_7_cout));
  Adder #(.width(1)) adder_8 (.a(A7), .b(xor_8_out), .out(S7), .cin(adder_7_cout), .cout(COUNT));

  // Notes on the sheet:
  //   K
  //   C1
  //   C2
  //   C3
  //   C4
  //   C5
  //   C6
  //   C7
endmodule
