// Logisim project 8bbit_sequential_counter.circ as structural Verilog: 1 circuit, main circuit main
module main (
  input  in_1,
  input  [7:0] in_2,
  input  in_3,
  output [7:0] out_4
);

  wire clock_1_out, not_1_out;
  wire [7:0] adder_1_out, buffer_1_out;

  assign buffer_1_out = adder_1_out;  // Buffer buffer_1, 8 bits wide
  not not_1 (not_1_out, in_1);
  assign buffer_1_out = in_2;  // Buffer buffer_2, 8 bits wide
  Clock clock_1 (.out(clock_1_out));
  Counter counter_1 (.D(buffer_1_out), .Q(out_4), .clk(clock_1_out), .clr(in_3));  // open: load, count, carry
  Adder adder_1 (.a(out_4), .b({8{1'b1}}), .out(adder_1_out));  // open: cin, cout
endmodule
