// Logisim project 8bitsregisters.circ as structural Verilog: 1 circuit, main circuit main
module main (
  input  [7:0] in_1,
  input  in_2,
  input  in_3,
  input  in_4,
  output [7:0] out_5
);

  Register register_1 (.D(in_1), .en(in_2), .Q(out_5), .clk(in_3), .clr(in_4));
endmodule
