// Logisim project 8to1bitMUX.circ as structural Verilog: 1 circuit, main circuit main
module main (
  input  in_1,
  input  in_2,
  input  in_3,
  input  in_4,
  input  in_5,
  input  in_6,
  input  in_7,
  input  in_8,
  input  in_9,
  input  [1:0] in_10,
  output out_11
);

  wire multiplexer_1_out, multiplexer_2_out;

  Multiplexer #(.select(2)) multiplexer_1 (
    .in0(in_1), .in1(in_2), .in2(in_3), .in3(in_4), .out(multiplexer_1_out), .sel(in_10), .en(in_9));
  Multiplexer #(.select(2)) multiplexer_2 (
    .in0(in_5), .in1(in_6), .in2(in_7), .in3(in_8), .out(multiplexer_2_out), .sel(in_10), .en(in_9));
  or or_1 (out_11, multiplexer_1_out, multiplexer_2_out);
endmodule
