// Logisim project ABLatch(NAND_gate).circ as structural Verilog: 1 circuit, main circuit main
module main (
  input  A,
  input  B,
  output C,
  output C_prime
);

  nand nand_1 (C, A, C_prime);
  nand nand_2 (C_prime, C, B);

  // Notes on the sheet:
  //   A  B  C  C'
  //   0  0  1  1
  //   1  0  0  1
  //   0  1  1  0
  //   1  1  1  0
endmodule
