// Logisim project ALU.circ as structural Verilog: 1 circuit, main circuit main
module main (
  input  in_1,
  input  in_2,
  input  in_3,
  input  [1:0] in_4,
  output out_5,
  output out_6
);

  wire adder_1_out, and_1_out, and_2_out, not_1_out, or_1_out, xor_1_out;

  xor xor_1 (xor_1_out, in_2, in_3);
  and and_1 (and_1_out, in_1, in_2);
  or or_1 (or_1_out, in_1, in_2);
  not not_1 (not_1_out, in_1);
  Adder #(.width(1)) adder_1 (.a(in_1), .b(xor_1_out), .out(adder_1_out), .cin(in_3), .cout(out_6));
  and and_2 (and_2_out, not_1_out, in_3);
  Multiplexer #(.select(2)) multiplexer_1 (
    .in1(or_1_out), .in2(adder_1_out), .in3(and_2_out), .out(out_5), .sel(in_4));  // open: in0, en
endmodule
