// Logisim project CAR SECURITY SYSTEM.circ as structural Verilog: 1 circuit, main circuit main
module main (
  input  ENGINE,
  input  K,
  input  D,
  input  KD_prime_KS_prime,
  input  S
);

  wire and_2_out, and_3_out, not_1_out, not_2_out;

  not not_1 (not_1_out, D);
  not not_2 (not_2_out, S);
  and and_1 (ENGINE, K, D, S);
  and and_2 (and_2_out, K, not_1_out);
  and and_3 (and_3_out, K, not_2_out);
  or or_1 (KD_prime_KS_prime, and_2_out, and_3_out);

  // Notes on the sheet:
  //   D'
  //   S'
  //   CAR SECURITY SYSTEM
  //   KDS
  //   KD'
  //   KS'
  //   BUZZER
endmodule
