// Logisim project Comparators.circ as structural Verilog: 1 circuit, main circuit main
module main (
  input  [6:0] in_1,
  output out_2,
  output I_type,
  output out_4,
  output Store,
  output Branch,
  output Jal,
  output Jalr,
  output Lui,
  output Auipc
);

  Comparator #(.width(7)) comparator_1 (.a(in_1), .b(7'b0110011), .eq(out_2));  // open: gt, lt
  Comparator #(.width(7)) comparator_2 (.a(in_1), .b(7'b0010011), .eq(I_type));  // open: gt, lt
  Comparator comparator_3 (.eq(out_4));  // open: a, b, gt, lt
  Comparator #(.width(7)) comparator_4 (.a(in_1), .b(7'b0100011), .eq(Store));  // open: gt, lt
  Comparator #(.width(7)) comparator_5 (.a(in_1), .b(7'b1100011), .eq(Branch));  // open: gt, lt
  Comparator #(.width(7)) comparator_6 (.a(in_1), .b(7'b1101111), .eq(Jal));  // open: gt, lt
  Comparator #(.width(7)) comparator_7 (.a(in_1), .b(7'b1100111), .eq(Jalr));  // open: gt, lt
  Comparator #(.width(7)) comparator_8 (.a(in_1), .b(7'b0110111), .eq(Lui));  // open: gt, lt
  Comparator #(.width(7)) comparator_9 (.a(in_1), .b(7'b0010111), .eq(Auipc));  // open: gt, lt

  // Notes on the sheet:
  //   R-format
  //   Load
endmodule
