// Logisim project D_Latch(NAND).circ as structural Verilog: 1 circuit, main circuit main
module main (
  input  S,
  input  R,
  output S_prime,
  output Q,
  output Q_prime,
  output R_prime
);

  wire not_1_out;

  not not_1 (not_1_out, S);
  nand nand_1 (S_prime, S, R);
  nand nand_2 (R_prime, R, not_1_out);
  nand nand_3 (Q, S_prime, Q_prime);
  nand nand_4 (Q_prime, Q, R_prime);

  // Notes on the sheet:
  //   S  R  S'  R'  Q  Q'
  //   0   0   1   1   0   1
  //   0   1   1   0   0   1
  //   1   0   1   1   1   0
  //   1   1   0   1   1   0
endmodule
