// Logisim project FSM using a D Flip-flop.circ as structural Verilog: 1 circuit, main circuit main
module main (
  input  in_1,
  input  in_2,
  output out_3
);

  wire clock_1_out, nand_1_out, xor_1_out;

  xor xor_1 (xor_1_out, in_1, in_2);
  nand nand_1 (nand_1_out, xor_1_out, out_3);
  Clock clock_1 (.out(clock_1_out));
  D_Flip_Flop d_ff_1 (.clk(nand_1_out), .D(clock_1_out), .Q(out_3));  // open: Qn, preset, en, reset
endmodule
