// Logisim project FULL SUBTRACTOR.circ as structural Verilog: 1 circuit, main circuit main
module main (
  input  Bin,
  input  A,
  input  B,
  output D,
  output Bout
);

  wire and_1_out, and_2_out, not_1_out, not_2_out, xor_1_out;

  not not_1 (not_1_out, A);
  xor xor_1 (xor_1_out, A, B);
  and and_1 (and_1_out, B, not_1_out);
  not not_2 (not_2_out, xor_1_out);
  and and_2 (and_2_out, not_2_out, Bin);
  xor xor_2 (D, Bin, xor_1_out);
  or or_1 (Bout, and_2_out, and_1_out);
endmodule
