// Logisim project JK_flipflop.circ as structural Verilog: 1 circuit, main circuit main
module main (
  input  in_1,
  input  in_2,
  output out_3,
  output out_4,
  output out_5,
  output out_6
);

  wire clock_1_out;

  Clock clock_1 (.out(clock_1_out));
  nand nand_1 (out_3, out_5, in_1, clock_1_out);
  nand nand_2 (out_6, clock_1_out, in_2, out_4);
  J_K_Flip_Flop j_k_ff_1 ();  // open: J, clk, K, Q, Qn, preset, en, reset
  nand nand_3 (out_4, out_3, out_5);
  nand nand_4 (out_5, out_4, out_6);
endmodule
