// Logisim project KMAP.circ as structural Verilog: 1 circuit, main circuit main
module main (
  input  A,
  input  B,
  input  C,
  input  D,
  input  in_5
);

  wire and_1_out, and_2_out, and_3_out, and_4_out, not_1_out, not_2_out, not_3_out;

  not not_1 (not_1_out, B);
  not not_2 (not_2_out, D);
  not not_3 (not_3_out, A);
  and and_1 (and_1_out, A, C);
  and and_2 (and_2_out, C, D);
  and and_3 (and_3_out, not_1_out, not_2_out);
  and and_4 (and_4_out, not_3_out, B, D);
  or or_1 (in_5, and_1_out, and_2_out, and_3_out, and_4_out);

  // Notes on the sheet:
  //   ___
  //   -
  //   F=AC+CD+BD+ABD
endmodule
