// Logisim project L2.circ as structural Verilog: 1 circuit, main circuit main
module main (
  input  D,
  input  M,
  input  S,
  input  in_4,
  input  in_5,
  input  in_6,
  output L,
  output out_8
);

  wire and_1_out;

  and and_1 (and_1_out, D, M);
  and and_2 (out_8, in_4, in_5, in_6);
  or or_1 (L, and_1_out, S);

  // Notes on the sheet:
  //   MD
endmodule
