// Logisim project L3.circ as structural Verilog: 1 circuit, main circuit main
module main (
  input  A,
  input  B,
  input  C,
  input  D,
  output A_prime_C_B_prime_D_prime_CD_A_prime_BD
);

  wire and_1_out, and_2_out, and_3_out, and_4_out, not_1_out, not_2_out, not_3_out;

  not not_1 (not_1_out, A);
  not not_2 (not_2_out, B);
  not not_3 (not_3_out, D);
  and and_1 (and_1_out, not_1_out, C);
  and and_2 (and_2_out, not_2_out, not_3_out);
  and and_3 (and_3_out, C, B);
  and and_4 (and_4_out, not_1_out, B, D);
  or or_1 (A_prime_C_B_prime_D_prime_CD_A_prime_BD, and_1_out, and_2_out, and_4_out, and_3_out);

  // Notes on the sheet:
  //   A'
  //   B'
  //   D'
  //   A'C
  //   CD
  //   A'BD
  //   B'D'
endmodule
