// Logisim project NAND universality.circ as structural Verilog: 1 circuit, main circuit main
module main (
  input  A,
  input  A_2,
  input  NAND_GATE_SYMBOL,
  input  A_3,
  input  B,
  input  A_4,
  input  A_B,
  input  A_5,
  input  B_2,
  input  A_6,
  input  A_7,
  input  A_B_2,
  input  A_8,
  input  Q,
  input  B_3,
  input  B_4,
  input  A_9,
  input  A_10,
  input  B_5,
  input  Q_2,
  input  A_B_3,
  input  B_6
);

  wire nand_2_out, nand_3_out, nand_4_out, nand_5_out, nand_6_out, nand_9_out, nand_11_out, nand_13_out,
       nand_14_out, nand_15_out, nand_16_out, nand_18_out, nand_19_out, nand_20_out;

  nand nand_1 (NAND_GATE_SYMBOL, A, B);
  nand nand_2 (nand_2_out, A_4, B_2);
  nand nand_3 (nand_3_out, A_7, A_7);
  nand nand_4 (nand_4_out, B_3, B_3);
  nand nand_5 (nand_5_out, A_9, A_9);
  nand nand_6 (nand_6_out, B_6, B_6);
  nand nand_7 (A_B, nand_2_out, nand_2_out);
  nand nand_8 (A_B_2, nand_3_out, nand_4_out);
  nand nand_9 (nand_9_out, nand_5_out, nand_6_out);
  nand nand_10 (A_B_3, nand_9_out, nand_9_out);
  nand nand_11 (nand_11_out, A_8, B_4);
  nand nand_12 (A_3, A_2, A_2);
  nand nand_13 (nand_13_out, A_5, A_5);
  nand nand_14 (nand_14_out, A_10, B_5);
  nand nand_15 (nand_15_out, A_10, A_10);
  nand nand_16 (nand_16_out, B_5, B_5);
  nand nand_17 (A_6, nand_13_out, nand_13_out);
  nand nand_18 (nand_18_out, A_8, nand_11_out);
  nand nand_19 (nand_19_out, nand_11_out, B_4);
  nand nand_20 (nand_20_out, nand_15_out, nand_16_out);
  nand nand_21 (Q, nand_18_out, nand_19_out);
  nand nand_22 (Q_2, nand_14_out, nand_20_out);

  // Notes on the sheet:
  //   AND GATE
  //   ___
  //   A.B
  //   OR GATE
  //   -
  //   A
  //   -
  //   B
  //   -
  //   A
  //   -
  //   B
  //   Q
  //   NOR GATE
  //   A+B
  //   ___
  //   NOT GATE
  //   (inverter)
  //   buffer
  //   _
  //   A
  //   _
  //   exclusive-OR
  //   exclusive-NOR
endmodule
