// Logisim project NOR universality.circ as structural Verilog: 1 circuit, main circuit main
module main (
  input  A,
  input  A_2,
  input  A_3,
  input  in_4,
  input  B,
  input  A_4,
  input  A_5,
  input  A_6,
  input  A_B,
  input  B_2,
  input  A_7,
  input  A_8,
  input  B_3,
  input  A_B_2,
  input  Q,
  input  B_4,
  input  A_9,
  input  A_B_3,
  input  B_5,
  input  A_10,
  input  Q_2,
  input  B_6
);

  wire nor_2_out, nor_3_out, nor_4_out, nor_5_out, nor_6_out, nor_9_out, nor_12_out, nor_13_out, nor_14_out,
       nor_15_out, nor_17_out, nor_18_out, nor_19_out, nor_20_out;

  nor nor_1 (in_4, A_2, B);
  nor nor_2 (nor_2_out, A_5, B_2);
  nor nor_3 (nor_3_out, A_8, A_8);
  nor nor_4 (nor_4_out, B_4, B_4);
  nor nor_5 (nor_5_out, A_9, A_9);
  nor nor_6 (nor_6_out, B_5, B_5);
  nor nor_7 (A_B, nor_2_out, nor_2_out);
  nor nor_8 (A_B_2, nor_3_out, nor_4_out);
  nor nor_9 (nor_9_out, nor_5_out, nor_6_out);
  nor nor_10 (A_B_3, nor_9_out, nor_9_out);
  nor nor_11 (A_3, A, A);
  nor nor_12 (nor_12_out, A_4, A_4);
  nor nor_13 (nor_13_out, A_7, A_7);
  nor nor_14 (nor_14_out, B_3, B_3);
  nor nor_15 (nor_15_out, A_10, B_6);
  nor nor_16 (A_6, nor_12_out, nor_12_out);
  nor nor_17 (nor_17_out, A_7, B_3);
  nor nor_18 (nor_18_out, nor_13_out, nor_14_out);
  nor nor_19 (nor_19_out, A_10, nor_15_out);
  nor nor_20 (nor_20_out, nor_15_out, B_6);
  nor nor_21 (Q, nor_17_out, nor_18_out);
  nor nor_22 (Q_2, nor_19_out, nor_20_out);

  // Notes on the sheet:
  //   NOR GATE SYMBOL
  //   OR GATE
  //   Q=A+B
  //   ____
  //   A+B
  //   AND GATE
  //   _
  //   A
  //   _
  //   B
  //   NAND GATE
  //   _
  //   A
  //   -
  //   B
  //   A.B
  //   ___
  //   NOT GATE
  //   (inverter)
  //   BUFFER
  //   -
  //   A
  //   Exclusive-OR
  //   -
  //   A
  //   -
  //   B
  //   _
  //   A.B
  //   Exclusive-NOR
  //   ___
  //   A+B
  //   ___
  //   A+B
  //   -
  //   A.B
  //   -
  //   A.B
endmodule
