// Logisim project PROGRAM_COUNTER.circ as structural Verilog: 1 circuit, main circuit main
module main (
  input  [31:0] in_1,
  output [31:0] out_2,
  output [31:0] out_3
);

  wire clk_t;

  Clock clock_1 (.out(clk_t));
  Register #(.width(32)) register_1 (.D(in_1), .en(1'b1), .Q(out_2), .clk(clk_t));  // open: clr
  Adder #(.width(32)) adder_1 (.a(out_2), .b(32'h32), .out(out_3));  // open: cin, cout

  // Other names for the same wires on the sheet: inPC_t[31:0] = in_1; outPC_t[31:0] = out_2;
  //   outPCPlus32_t[31:0] = out_3
endmodule
