// Logisim project Risc V.circ as structural Verilog
module main (
  input  [31:0] in_1,
  input  [31:0] in_2,
  output [31:0] out_3,
  output [31:0] out_4,
  output [31:0] out_5,
  output [31:0] out_6,
  output [31:0] out_7
);

  wire [19:0] shifter_1_out;
  wire [31:0] bit_extender_3_out, bit_extender_4_out;

  Shifter #(.width(20)) shifter_1 (.in(in_2[31:12]), .\dist (5'b01100), .out(shifter_1_out));
  assign out_3 = {{20{in_2[31]}}, in_2[31:20]};  // Bit_Extender bit_extender_1
  assign out_4 = {{20{in_2[31]}}, {in_2[31:25], in_2[11:7]}};  // Bit_Extender bit_extender_2
  assign bit_extender_3_out = {{19{in_2[31]}}, {in_2[31], in_2[7], in_2[30:25], in_2[11:8], 1'b0}};  // Bit_Extender bit_extender_3
  assign bit_extender_4_out = {{11{in_2[31]}}, {in_2[31], in_2[19:12], in_2[20], in_2[30:21], 1'b0}};  // Bit_Extender bit_extender_4
  assign out_7 = {{12{shifter_1_out[19]}}, shifter_1_out};  // Bit_Extender bit_extender_5
  Adder #(.width(32)) adder_1 (.a(bit_extender_3_out), .b(in_1), .out(out_5));  // open: cin, cout
  Adder #(.width(32)) adder_2 (.a(bit_extender_4_out), .b(in_1), .out(out_6));  // open: cin, cout

  // Notes on the sheet:
  //   I-Type
  //   S-Type
  //   Sb-Type
  //   UJ-Type
  //   U-Type
endmodule

module Imm_Gen (
  input  [31:0] in_1,
  input  [31:0] in_2,
  output [31:0] out_3,
  output [31:0] out_4,
  output [31:0] out_5,
  output [31:0] out_6,
  output [31:0] out_7
);

  wire [19:0] shifter_1_out;
  wire [31:0] bit_extender_3_out, bit_extender_4_out;

  Shifter #(.width(20)) shifter_1 (.in(in_2[31:12]), .\dist (5'b01100), .out(shifter_1_out));
  assign out_3 = {{20{in_2[31]}}, in_2[31:20]};  // Bit_Extender bit_extender_1
  assign out_4 = {{20{in_2[31]}}, {in_2[31:25], in_2[11:7]}};  // Bit_Extender bit_extender_2
  assign bit_extender_3_out = {{19{in_2[31]}}, {in_2[31], in_2[7], in_2[30:25], in_2[11:8], 1'b0}};  // Bit_Extender bit_extender_3
  assign bit_extender_4_out = {{11{in_2[31]}}, {in_2[31], in_2[19:12], in_2[20], in_2[30:21], 1'b0}};  // Bit_Extender bit_extender_4
  assign out_7 = {{12{shifter_1_out[19]}}, shifter_1_out};  // Bit_Extender bit_extender_5
  Adder #(.width(32)) adder_1 (.a(bit_extender_3_out), .b(in_1), .out(out_5));  // open: cin, cout
  Adder #(.width(32)) adder_2 (.a(bit_extender_4_out), .b(in_1), .out(out_6));  // open: cin, cout

  // Notes on the sheet:
  //   I-Type
  //   S-Type
  //   Sb-Type
  //   UJ-Type
  //   U-Type
endmodule
