// Logisim project SAMRT LIGHTING.circ as structural Verilog: 1 circuit, main circuit main
module main (
  input  S,
  input  L,
  input  M,
  input  D
);

  wire and_1_out;

  and and_1 (and_1_out, M, D);
  or or_1 (L, S, and_1_out);

  // Notes on the sheet:
  //   SAMRT LIGHTING PROBLEM
  //   MD
  //   S+MD
endmodule
