// Logisim project SR_Latch.circ as structural Verilog: 1 circuit, main circuit main
module main (
  input  in_1,
  input  in_2,
  output Q,
  output Q_prime
);

  nand nand_1 (Q, in_1, Q_prime);
  nand nand_2 (Q_prime, Q, in_2);
endmodule
