// Logisim project SR_NOR_Latch.circ as structural Verilog: 1 circuit, main circuit main
module main (
  input  R,
  input  S,
  output Q,
  output Q_prime
);

  nor nor_1 (Q, R, Q_prime);
  nor nor_2 (Q_prime, Q, S);

  // Notes on the sheet:
  //   R  S  Q  Q'
  //   0  0  0  1
  //   0  1  1  0
  //   1  0  0  1
  //   1  1  0  0
endmodule
