// Logisim project decoder.circ as structural Verilog: 1 circuit, main circuit main
module main (
  input  A,
  input  B,
  input  in_3,
  input  [1:0] in_4,
  input  in_5,
  input  in_6,
  input  in_7,
  output out_8,
  output out_9,
  output out_10,
  output out_11,
  output out_12,
  output out_13,
  output out_14,
  output out_15,
  output out_16,
  output out_17,
  output out_18,
  output out_19,
  output out_20,
  output out_21,
  output out_22,
  output out_23
);

  wire not_1_out, not_2_out, not_3_out, not_4_out, not_5_out;

  not not_1 (not_1_out, A);
  not not_2 (not_2_out, B);
  not not_3 (not_3_out, in_5);
  not not_4 (not_4_out, in_6);
  not not_5 (not_5_out, in_7);
  and and_1 (out_9, not_1_out, not_2_out);
  and and_2 (out_12, not_1_out, B);
  and and_3 (out_14, A, not_2_out);
  and and_4 (out_15, A, B);
  and and_5 (out_16, not_3_out, not_4_out, not_5_out);
  and and_6 (out_17, not_3_out, not_4_out, in_7);
  and and_7 (out_18, not_3_out, in_6, not_5_out);
  and and_8 (out_19, not_3_out, in_6, in_7);
  and and_9 (out_20, in_5, not_4_out, not_5_out);
  and and_10 (out_21, in_5, not_4_out, in_7);
  and and_11 (out_22, in_5, in_6, not_5_out);
  and and_12 (out_23, in_5, in_6, in_7);
  Decoder #(.select(2)) decoder_1 (.out0(out_8), .out1(out_10), .out2(out_11), .out3(out_13), .sel(in_4), .en(in_3));

  // Notes on the sheet:
  //   2:4 Decoder
  //   3:8Decoder
  //   A'B
  //   AB'
  //   A'B'
  //   AB
endmodule
