// Logisim project gates assign.circ as structural Verilog: 1 circuit, main circuit main
module main (
  input  in_1,
  input  in_2,
  output out_3,
  output out_4,
  output out_5,
  output out_6,
  output out_7,
  output out_8
);

  wire not_1_out;

  not not_1 (not_1_out, in_2);
  not not_2 (out_5, in_1);
  or or_1 (out_3, in_1, not_1_out);
  and and_1 (out_4, in_1, not_1_out);
  nor nor_1 (out_6, in_2, in_1);
  nand nand_1 (out_7, in_1, in_2);
  xnor xnor_1 (out_8, in_1, in_2);
endmodule
