// Logisim project kmap2.circ as structural Verilog: 1 circuit, main circuit main
module main (
  input  A,
  input  B,
  input  C,
  input  in_4,
  input  D
);

  wire and_1_out, and_2_out, and_3_out, not_1_out, not_2_out, not_3_out;

  not not_1 (not_1_out, A);
  not not_2 (not_2_out, B);
  not not_3 (not_3_out, D);
  and and_1 (and_1_out, not_1_out, C);
  and and_2 (and_2_out, C, D);
  and and_3 (and_3_out, not_2_out, not_3_out);
  or or_1 (in_4, and_1_out, and_2_out, and_3_out);

  // Notes on the sheet:
  //   F=B'D'+A'C+CD
  //   m(0,2,3,6,8,10,15)+d(11)
endmodule
