// Logisim project l1.circ as structural Verilog: 1 circuit, main circuit main
module main (
  input  in_1,
  input  in_2,
  output out_3
);

  wire and_1_out, nand_1_out, nor_1_out, not_1_out, not_2_out, or_1_out;

  not not_1 (not_1_out, in_1);
  not not_2 (not_2_out, in_2);
  nand nand_1 (nand_1_out, not_1_out, in_2);
  nor nor_1 (nor_1_out, in_1, not_2_out);
  and and_1 (and_1_out, nand_1_out, in_1);
  or or_1 (or_1_out, in_2, nor_1_out);
  xor xor_1 (out_3, and_1_out, or_1_out);
endmodule
