// Logisim project logic gates verification.circ as structural Verilog
module main (
  input  in_1,
  input  in_2,
  input  in_3,
  input  OR_GATE,
  input  BUFFER,
  input  in_6,
  input  in_7,
  input  in_8,
  input  in_9,
  input  in_10,
  input  in_11,
  input  in_12,
  input  in_13,
  input  in_14,
  output out_15,
  output out_16,
  output out_17,
  output out_18,
  output out_19,
  output out_20,
  output out_21,
  output out_22
);

  or or_1 (out_16, in_2, OR_GATE);
  nand nand_1 (out_18, in_6, in_7);
  nor nor_1 (out_20, in_9, in_11);
  xor xor_1 (out_22, in_13, in_14);
  and and_1 (out_15, in_1, in_3);
  buf buffer_1 (out_17, BUFFER);
  not not_1 (out_19, in_8);
  xnor xnor_1 (out_21, in_10, in_12);

  // Notes on the sheet:
  //   NAND GATE
  //   NOR GATE
  //   XOR GATE
  //   AND GATE
  //   NOT GATE
  //   XNOR GATE
endmodule
