// Logisim project traffic_light.circ as structural Verilog: 1 circuit, main circuit main
module main (
);

  wire and_1_out, button_1_out, clock_1_out, clock_2_out, comparator_1_eq, undriven;
  wire [2:0] counter_1_q, rom_1_data, rom_2_data;
  wire [5:0] counter_2_q;

  Clock clock_1 (.out(clock_1_out));
  Button button_1 (.out(button_1_out));
  Clock clock_2 (.out(clock_2_out));
  Counter #(.width(3), .max('h7)) counter_1 (
    .count(clock_1_out), .Q(counter_1_q), .clk(clock_1_out), .clr(button_1_out));  // open: load, D, carry
  and and_1 (and_1_out, 1'b1, comparator_1_eq);
  Comparator #(.width(6)) comparator_1 (.a(counter_2_q), .b(6'b110010), .eq(comparator_1_eq));  // open: gt, lt
  Counter #(.width(6), .max('h3f)) counter_2 (
    .count(clock_2_out), .Q(counter_2_q), .clk(clock_2_out), .clr(and_1_out));  // open: load, D, carry
  ROM #(.addrWidth(3), .dataWidth(3)) rom_1 (.addr(counter_1_q), .data(rom_1_data));  // open: sel
  ROM #(.addrWidth(6), .dataWidth(3)) rom_2 (.addr(counter_2_q), .data(rom_2_data));  // open: sel
  LED led_1 (.in(rom_1_data[0]));
  LED led_2 (.in(rom_1_data[1]));
  LED led_3 (.in(rom_1_data[2]));
  LED led_4 (.in(rom_2_data[0]));
  LED led_5 (.in(rom_2_data[2]));
  LED led_6 (.in(undriven));

  // Notes on the sheet:
  //   RED LED TURN ON FOR 30SEC
  //   ORANGE TURN ON FOR 5SEC
  //   GREEN TURN ON FOR 35SEC
  //   contents of rom_1 (hex, n*v repeats v):
  //   1 3 2 4 0 4 2 1
  //   contents of rom_2 (hex, n*v repeats v):
  //   30*1 2 2 5*4 2 2
endmodule
